// Logisim project Proyecto2Circuito.circ as structural Verilog: 7 circuits, main circuit main
module main (
  input  [7:0] A,
  input  [7:0] B,
  input  [1:0] in_3,
  output [7:0] S,
  output out_5,
  output Sign,
  output out_7
);

  wire [7:0] not_1_out, sumador_8bit_1_s;

  not not_1 (not_1_out[0], A[0]);
  not not_2 (not_1_out[1], A[1]);
  not not_3 (not_1_out[2], A[2]);
  not not_4 (not_1_out[3], A[3]);
  not not_5 (not_1_out[4], A[4]);
  not not_6 (not_1_out[5], A[5]);
  not not_7 (not_1_out[6], A[6]);
  not not_8 (not_1_out[7], A[7]);
  sumador_8bit sumador_8bit_1 (.A(A), .B(B), .S_R(in_3[0]), .S(sumador_8bit_1_s), .Co(out_7));
  MUX4_8bit mux4_8bit_1 (
    .A_B(sumador_8bit_1_s), .C(not_1_out), .D({A[6:0], A[7]}), .OP0(in_3[0]), .OP1(in_3[1]), .S(S));
  Zero zero_1 (.in_1(S), .Z(out_5));

  assign Sign = S[7];
endmodule

module SUM4 (
  input  [3:0] A,
  input  [3:0] B,
  input  Ce,
  output [3:0] S,
  output Cs
);

  _74283 #(.ShowInternalStructure("true")) u_74283_1 (
    .pin1(S[1]), .pin2(B[1]), .pin3(A[1]), .pin4(S[0]), .pin5(A[0]), .pin6(B[0]), .pin7(Ce), .pin15(B[2]),
    .pin14(A[2]), .pin13(S[2]), .pin12(A[3]), .pin11(B[3]), .pin10(S[3]), .pin9(Cs));
endmodule

module SUM8 (
  input  Ce,
  input  [7:0] A,
  input  [7:0] B,
  output [7:0] S,
  output Cs
);

  wire sum4_1_cs;

  SUM4 sum4_1 (.A(A[3:0]), .B(B[3:0]), .Ce(Ce), .S(S[3:0]), .Cs(sum4_1_cs));
  SUM4 sum4_2 (.A(A[7:4]), .B(B[7:4]), .Ce(sum4_1_cs), .S(S[7:4]), .Cs(Cs));
endmodule

module Complemento (
  input  [7:0] B,
  input  Op,
  output [7:0] S
);

  _7486 #(.ShowInternalStructure("true")) u_7486_1 (
    .pin1(B[7]), .pin2(Op), .pin3(S[7]), .pin4(B[6]), .pin5(Op), .pin6(S[6]), .pin13(B[5]), .pin12(Op),
    .pin11(S[5]), .pin10(B[4]), .pin9(Op), .pin8(S[4]));
  _7486 #(.ShowInternalStructure("true")) u_7486_2 (
    .pin1(B[3]), .pin2(Op), .pin3(S[3]), .pin4(B[2]), .pin5(Op), .pin6(S[2]), .pin13(B[1]), .pin12(Op),
    .pin11(S[1]), .pin10(B[0]), .pin9(Op), .pin8(S[0]));
endmodule

module sumador_8bit (
  input  [7:0] A,
  input  [7:0] B,
  input  S_R,
  output [7:0] S,
  output Co
);

  wire [7:0] complemento_1_s;

  SUM8 sum8_1 (.Ce(S_R), .A(A), .B(complemento_1_s), .S(S), .Cs(Co));
  Complemento complemento_1 (.B(B), .Op(S_R), .S(complemento_1_s));
endmodule

module MUX4_8bit (
  input  [7:0] A_B,
  input  [7:0] C,
  input  [7:0] D,
  input  OP0,
  input  OP1,
  output [7:0] S
);

  wire [3:0] multiplexer_1_out, multiplexer_2_out;

  Multiplexer #(.enable("true"), .width(4)) multiplexer_1 (
    .in0(C[3:0]), .in1(D[3:0]), .out(multiplexer_1_out), .sel(OP0), .en(1'b1));
  Multiplexer #(.enable("true"), .width(4)) multiplexer_2 (
    .in0(C[7:4]), .in1(D[7:4]), .out(multiplexer_2_out), .sel(OP0), .en(1'b1));
  Multiplexer #(.enable("true"), .width(4)) multiplexer_3 (
    .in0(A_B[3:0]), .in1(multiplexer_1_out), .out(S[3:0]), .sel(OP1), .en(1'b1));
  Multiplexer #(.enable("true"), .width(4)) multiplexer_4 (
    .in0(A_B[7:4]), .in1(multiplexer_2_out), .out(S[7:4]), .sel(OP1), .en(1'b1));
endmodule

module Zero (
  input  [7:0] in_1,
  output Z
);

  wire or_1_out, or_2_out, or_3_out, or_4_out, or_5_out, or_6_out;

  or or_1 (or_1_out, in_1[0], in_1[1]);
  or or_2 (or_2_out, in_1[2], in_1[3]);
  or or_3 (or_3_out, in_1[4], in_1[5]);
  or or_4 (or_4_out, in_1[6], in_1[7]);
  or or_5 (or_5_out, or_1_out, or_2_out);
  or or_6 (or_6_out, or_3_out, or_4_out);
  nor nor_1 (Z, or_5_out, or_6_out);
endmodule
